// Logisim project seq_circuit.circ as structural Verilog: 1 circuit, main circuit main
module main (
);

  wire undriven, undriven_2, undriven_3, undriven_4, xor_1_out, xor_2_out;

  xor xor_1 (xor_1_out, undriven_3, undriven_4);
  ExactlyOne xor_2 (.out(xor_2_out), .in0(undriven), .in1(undriven_2), .in2(xor_1_out));

  // Notes on the sheet:
  //   x
  //   y
  //   D'
  //   D
  //   C
  //   S
endmodule
